// Logisim project nibadder.circ as structural Verilog: 1 circuit, main circuit main
module main (
  input  CIN,
  input  [3:0] inputA,
  input  [3:0] inputB,
  output [3:0] AplusB,
  output COUT
);

  wire and_1_out, and_2_out, and_3_out, and_4_out, and_5_out, and_6_out, and_7_out, and_8_out, and_9_out,
       and_10_out, and_11_out, and_12_out, c1_out, c2_out, c3_out, or_1_out, or_2_out, or_3_out, or_4_out,
       xor_1_out, xor_2_out, xor_3_out, xor_4_out;

  xor xor_1 (xor_1_out, CIN, inputA[0]);
  and and_1 (and_1_out, inputA[0], CIN);
  and and_2 (and_2_out, inputB[0], CIN);
  and and_3 (and_3_out, inputB[0], inputA[0]);
  xor xor_2 (xor_2_out, inputA[1], c1_out);
  and and_4 (and_4_out, inputA[1], c1_out);
  and and_5 (and_5_out, c1_out, inputB[1]);
  and and_6 (and_6_out, inputA[1], inputB[1]);
  xor xor_3 (xor_3_out, c2_out, inputA[2]);
  and and_7 (and_7_out, c2_out, inputA[2]);
  and and_8 (and_8_out, c2_out, inputB[2]);
  and and_9 (and_9_out, inputA[2], inputB[2]);
  xor xor_4 (xor_4_out, c3_out, inputA[3]);
  and and_10 (and_10_out, c3_out, inputA[3]);
  and and_11 (and_11_out, c3_out, inputB[3]);
  and and_12 (and_12_out, inputA[3], inputB[3]);
  xor bit1 (AplusB[0], xor_1_out, inputB[0]);
  or or_1 (or_1_out, and_1_out, and_2_out);
  or c1 (c1_out, or_1_out, and_3_out);
  xor bit2 (AplusB[1], xor_2_out, inputB[1]);
  or or_2 (or_2_out, and_4_out, and_5_out);
  or c2 (c2_out, or_2_out, and_6_out);
  xor bit3 (AplusB[2], xor_3_out, inputB[2]);
  or or_3 (or_3_out, and_7_out, and_8_out);
  or c3 (c3_out, or_3_out, and_9_out);
  xor bit4 (AplusB[3], xor_4_out, inputB[3]);
  or or_4 (or_4_out, and_10_out, and_11_out);
  or c4 (COUT, or_4_out, and_12_out);

  // Notes on the sheet:
  //   I pledge my honor that I have abided by the Stevens Honor System
  //   Rohan Kallur
endmodule
