// Logisim project nibmux.circ as structural Verilog: 1 circuit, main circuit main
module main (
  input  Switch,
  input  [3:0] inputA,
  input  [3:0] inputB,
  output [3:0] AorB
);

  wire and_1_out, and_2_out, and_3_out, and_4_out, and_5_out, and_6_out, and_7_out, and_8_out, not_1_out;

  not not_1 (not_1_out, Switch);
  and and_1 (and_1_out, not_1_out, inputA[0]);
  and and_2 (and_2_out, Switch, inputB[0]);
  and and_3 (and_3_out, not_1_out, inputA[1]);
  and and_4 (and_4_out, Switch, inputB[2]);
  and and_5 (and_5_out, not_1_out, inputA[2]);
  and and_6 (and_6_out, Switch, inputB[2]);
  and and_7 (and_7_out, not_1_out, inputA[3]);
  and and_8 (and_8_out, Switch, inputB[3]);
  or Bit1 (AorB[0], and_1_out, and_2_out);
  or bit2 (AorB[1], and_3_out, and_4_out);
  or bit3 (AorB[2], and_5_out, and_6_out);
  or bit4 (AorB[3], and_7_out, and_8_out);

  assign inputB[1] = inputB[2];

  // Notes on the sheet:
  //   Rohan Kallur
  //   I pledge my honor that i have abided by the Stevens Honor System.
endmodule
